// Logisim project leticia_souza.circ as structural Verilog: 20 circuits, main circuit main
module main (
  input  c_in,
  input  in_2,
  input  [15:0] a_16bit,
  input  in_4,
  input  [15:0] b_16bit,
  output out_6,
  output out_7,
  output [15:0] o,
  output out_9,
  output out_10,
  output c_out
);

  wire adaptador_porta_1_to_ms, data_address, flag_1_out_6, flag_1_out_7, flag_1_out_8, flag_1_out_9,
       input_output, io_clk_s, io_e, monitor_adaptador_1_to_m, monitor_adaptador_1_to_ms, or_1_out,
       portio_1_p1, teclado_1_out_8, teclado_1_out_9, uc_1_out_6, uc_1_out_7, uc_1_out_8, uc_1_out_9,
       uc_1_out_10, uc_1_out_11, uc_1_out_12, uc_1_out_13, uc_1_out_14, uc_1_out_15, uc_1_out_17,
       uc_1_out_18, uc_1_out_19, uc_1_out_20, uc_1_out_21, uc_1_out_22, uc_1_out_25, uc_1_out_26,
       uc_1_out_27, uc_1_out_30, ula_1_a_equal_b, ula_1_a_larger_than_b, ula_1_carry_out, ula_1_zero;
  wire [2:0] uc_1_out_16;
  wire [6:0] keyboard_1_data, monitor_adaptador_1_out_5;
  wire [15:0] acc_q, bus1_o, controlled_buffer_7_out, IAR_q, IR_q, MAR_q, R0_q, R1_q, R2_q, R3_q,
       teclado_1_out_7, tmp_q, ula_1_out_5;

  Register #(.width(16)) tmp (.D(teclado_1_out_7), .Q(tmp_q), .clk(uc_1_out_6));  // open: en, clr
  bus_1 bus1 (.s(uc_1_out_7), .i(tmp_q), .o(bus1_o));
  ULA ula_1 (
    .A(teclado_1_out_7), .B(bus1_o), .out_5(ula_1_out_5), .in_1(uc_1_out_16), .carry_out(ula_1_carry_out),
    .A_larger_than_B(ula_1_a_larger_than_b), .A_equal_B(ula_1_a_equal_b), .zero(ula_1_zero));
  somador_16bit somador (.a_16bit(a_16bit), .b_16bit(b_16bit), .c_in(c_in), .c_out(c_out), .s_16bit(o));
  flag flag_1 (
    .in_1(ula_1_carry_out), .in_2(ula_1_a_larger_than_b), .in_3(ula_1_a_equal_b), .in_4(ula_1_zero),
    .out_6(flag_1_out_6), .out_7(flag_1_out_7), .out_8(flag_1_out_8), .out_9(flag_1_out_9), .in_5(uc_1_out_21));
  Register #(.width(16)) acc (.D(ula_1_out_5), .Q(acc_q), .clk(uc_1_out_25));  // open: en, clr
  teclado teclado_1 (
    .in_2(io_e), .in_4(io_clk_s), .in_5(data_address), .in_6(input_output), .in_1(teclado_1_out_7),
    .out_7(teclado_1_out_7), .in_3(keyboard_1_data), .out_8(teclado_1_out_8), .out_9(teclado_1_out_9));
  assign teclado_1_out_7 = uc_1_out_22 ? acc_q : 16'bz;  // Controlled_Buffer controlled_buffer_1
  Keyboard keyboard_1 (.clk(teclado_1_out_8), .re(teclado_1_out_9), .data(keyboard_1_data));  // open: clr, avail
  assign teclado_1_out_7 = uc_1_out_9 ? R0_q : 16'bz;  // Controlled_Buffer controlled_buffer_2
  Register #(.width(16)) R0 (.D(teclado_1_out_7), .Q(R0_q), .clk(uc_1_out_8));  // open: en, clr
  Register #(.width(16)) IAR (.D(teclado_1_out_7), .Q(IAR_q), .clk(uc_1_out_26));  // open: en, clr
  assign teclado_1_out_7 = uc_1_out_27 ? IAR_q : 16'bz;  // Controlled_Buffer controlled_buffer_3
  deco_2x4 d_2x4 (.in_1(in_2), .in_2(in_4), .out_3(out_6), .out_4(out_7), .out_5(out_9), .out_6(out_10));
  assign teclado_1_out_7 = uc_1_out_11 ? R1_q : 16'bz;  // Controlled_Buffer controlled_buffer_4
  Register #(.width(16)) R1 (.D(teclado_1_out_7), .Q(R1_q), .clk(uc_1_out_10));  // open: en, clr
  UC uc_1 (
    .out_16(uc_1_out_16), .in_1(flag_1_out_6), .in_2(flag_1_out_7), .in_3(flag_1_out_8), .in_4(flag_1_out_9),
    .out_21(uc_1_out_21), .out_6(uc_1_out_6), .out_7(uc_1_out_7), .out_8(uc_1_out_8), .out_9(uc_1_out_9),
    .out_10(uc_1_out_10), .out_11(uc_1_out_11), .out_12(uc_1_out_12), .out_13(uc_1_out_13),
    .out_14(uc_1_out_14), .out_15(uc_1_out_15), .out_25(uc_1_out_25), .out_22(uc_1_out_22),
    .out_26(uc_1_out_26), .out_27(uc_1_out_27), .out_30(uc_1_out_30), .in_5(IR_q), .out_23(input_output),
    .out_24(data_address), .out_28(io_e), .out_29(io_clk_s), .out_17(uc_1_out_17), .out_18(uc_1_out_18),
    .out_19(uc_1_out_19), .out_20(uc_1_out_20));
  LED led_1 (.in(uc_1_out_20));
  assign teclado_1_out_7 = uc_1_out_13 ? R2_q : 16'bz;  // Controlled_Buffer controlled_buffer_5
  Register #(.width(16)) R2 (.D(teclado_1_out_7), .Q(R2_q), .clk(uc_1_out_12));  // open: en, clr
  Register #(.width(16)) IR (.D(teclado_1_out_7), .Q(IR_q), .clk(uc_1_out_30));  // open: en, clr
  assign teclado_1_out_7 = uc_1_out_15 ? R3_q : 16'bz;  // Controlled_Buffer controlled_buffer_6
  Register #(.width(16)) R3 (.D(teclado_1_out_7), .Q(R3_q), .clk(uc_1_out_14));  // open: en, clr
  monitor_adaptador monitor_adaptador_1 (
    .io(input_output), .da(data_address), .ios(io_clk_s), .in_1(teclado_1_out_7),
    .out_5(monitor_adaptador_1_out_5), .to_ms(monitor_adaptador_1_to_ms), .to_m(monitor_adaptador_1_to_m));
  TTY tty_1 (
    .data(monitor_adaptador_1_out_5), .clk(monitor_adaptador_1_to_ms), .we(monitor_adaptador_1_to_m));  // open: clr
  Register #(.width(16)) MAR (.D(teclado_1_out_7), .Q(MAR_q), .clk(uc_1_out_17));  // open: en, clr
  or or_1 (or_1_out, uc_1_out_18, uc_1_out_19);
  RAM #(.addrWidth(16), .dataWidth(16), .databus("bidir"), .\type ("nonvolatile")) ram_1 (
    .addr(MAR_q), .we(uc_1_out_18), .oe(uc_1_out_19), .clk(or_1_out));  // open: data
  assign controlled_buffer_7_out = adaptador_porta_1_to_ms ? teclado_1_out_7 : 16'bz;  // Controlled_Buffer controlled_buffer_7
  // PortIO #(.number(16)) portio_1: pin names not known; wires that end beside it: portio_1_p1, controlled_buffer_7_out
  adaptador_porta adaptador_porta_1 (
    .io(input_output), .da(data_address), .ios(io_clk_s), .in_1(teclado_1_out_7),
    .to_ms(adaptador_porta_1_to_ms), .to_m(portio_1_p1));

  // Notes on the sheet:
  //   22450212
  //   Leticia Souza de Souza
endmodule

module enable (
  input  [7:0] in_1,
  input  e,
  output [7:0] out_3
);

  and and_1 (out_3[0], in_1[0], e);
  and and_2 (out_3[1], in_1[1], e);
  and and_3 (out_3[2], in_1[2], e);
  and and_4 (out_3[3], in_1[3], e);
  and and_5 (out_3[4], in_1[4], e);
  and and_6 (out_3[5], in_1[5], e);
  and and_7 (out_3[6], in_1[6], e);
  and and_8 (out_3[7], in_1[7], e);
endmodule

module somador_1bit (
  input  c_in,
  input  a,
  input  b,
  output c,
  output c_out
);

  wire and_1_out, and_2_out, and_3_out, xor_1_out;

  xor xor_1 (xor_1_out, a, b);
  and and_1 (and_1_out, a, c_in);
  and and_2 (and_2_out, a, b);
  and and_3 (and_3_out, b, c_in);
  or or_1 (c_out, and_1_out, and_2_out, and_3_out);
  xor xor_2 (c, xor_1_out, c_in);
endmodule

module somador_16bit (
  input  c_in,
  input  [15:0] a_16bit,
  input  [15:0] b_16bit,
  output [15:0] s_16bit,
  output c_out
);

  wire somador_1bit_1_c_out, somador_1bit_2_c_out, somador_1bit_3_c_out, somador_1bit_4_c_out,
       somador_1bit_5_c_out, somador_1bit_6_c_out, somador_1bit_7_c_out, somador_1bit_8_c_out,
       somador_1bit_9_c_out, somador_1bit_10_c_out, somador_1bit_11_c_out, somador_1bit_12_c_out,
       somador_1bit_13_c_out, somador_1bit_14_c_out, somador_1bit_15_c_out;

  somador_1bit somador_1bit_1 (
    .a(a_16bit[0]), .b(b_16bit[0]), .c_in(c_in), .c_out(somador_1bit_1_c_out), .c(s_16bit[0]));
  somador_1bit somador_1bit_2 (
    .a(a_16bit[1]), .b(b_16bit[1]), .c_in(somador_1bit_1_c_out), .c_out(somador_1bit_2_c_out), .c(s_16bit[1]));
  somador_1bit somador_1bit_3 (
    .a(a_16bit[2]), .b(b_16bit[2]), .c_in(somador_1bit_2_c_out), .c_out(somador_1bit_3_c_out), .c(s_16bit[2]));
  somador_1bit somador_1bit_4 (
    .a(a_16bit[3]), .b(b_16bit[3]), .c_in(somador_1bit_3_c_out), .c_out(somador_1bit_4_c_out), .c(s_16bit[3]));
  somador_1bit somador_1bit_5 (
    .a(a_16bit[4]), .b(b_16bit[4]), .c_in(somador_1bit_4_c_out), .c_out(somador_1bit_5_c_out), .c(s_16bit[4]));
  somador_1bit somador_1bit_6 (
    .a(a_16bit[5]), .b(b_16bit[5]), .c_in(somador_1bit_5_c_out), .c_out(somador_1bit_6_c_out), .c(s_16bit[5]));
  somador_1bit somador_1bit_7 (
    .a(a_16bit[6]), .b(b_16bit[6]), .c_in(somador_1bit_6_c_out), .c_out(somador_1bit_7_c_out), .c(s_16bit[6]));
  somador_1bit somador_1bit_8 (
    .a(a_16bit[7]), .b(b_16bit[7]), .c_in(somador_1bit_7_c_out), .c_out(somador_1bit_8_c_out), .c(s_16bit[7]));
  somador_1bit somador_1bit_9 (
    .a(a_16bit[8]), .b(b_16bit[8]), .c_in(somador_1bit_8_c_out), .c_out(somador_1bit_9_c_out), .c(s_16bit[8]));
  somador_1bit somador_1bit_10 (
    .a(a_16bit[9]), .b(b_16bit[9]), .c_in(somador_1bit_9_c_out), .c_out(somador_1bit_10_c_out), .c(s_16bit[9]));
  somador_1bit somador_1bit_11 (
    .a(a_16bit[10]), .b(b_16bit[10]), .c_in(somador_1bit_10_c_out), .c_out(somador_1bit_11_c_out),
    .c(s_16bit[10]));
  somador_1bit somador_1bit_12 (
    .a(a_16bit[11]), .b(b_16bit[11]), .c_in(somador_1bit_11_c_out), .c_out(somador_1bit_12_c_out),
    .c(s_16bit[11]));
  somador_1bit somador_1bit_13 (
    .a(a_16bit[12]), .b(b_16bit[12]), .c_in(somador_1bit_12_c_out), .c_out(somador_1bit_13_c_out),
    .c(s_16bit[12]));
  somador_1bit somador_1bit_14 (
    .a(a_16bit[13]), .b(b_16bit[13]), .c_in(somador_1bit_13_c_out), .c_out(somador_1bit_14_c_out),
    .c(s_16bit[13]));
  somador_1bit somador_1bit_15 (
    .a(a_16bit[14]), .b(b_16bit[14]), .c_in(somador_1bit_14_c_out), .c_out(somador_1bit_15_c_out),
    .c(s_16bit[14]));
  somador_1bit somador_1bit_16 (
    .a(a_16bit[15]), .b(b_16bit[15]), .c_in(somador_1bit_15_c_out), .c_out(c_out), .c(s_16bit[15]));
endmodule

module memoria_1bit (
  input  i,
  input  s,
  output o
);

  wire nand_1_out, nand_2_out, nand_4_out;

  nand nand_1 (nand_1_out, i, s);
  nand nand_2 (nand_2_out, nand_1_out, s);
  nand nand_3 (o, nand_1_out, nand_4_out);
  nand nand_4 (nand_4_out, o, nand_2_out);
endmodule

module memoria_8bit (
  input  [7:0] i_8bit,
  input  s,
  output [7:0] o_8bit
);

  memoria_1bit memoria_1bit_1 (.i(i_8bit[0]), .s(s), .o(o_8bit[0]));
  memoria_1bit memoria_1bit_2 (.i(i_8bit[1]), .s(s), .o(o_8bit[1]));
  memoria_1bit memoria_1bit_3 (.i(i_8bit[2]), .s(s), .o(o_8bit[2]));
  memoria_1bit memoria_1bit_4 (.i(i_8bit[3]), .s(s), .o(o_8bit[3]));
  memoria_1bit memoria_1bit_5 (.i(i_8bit[4]), .s(s), .o(o_8bit[4]));
  memoria_1bit memoria_1bit_6 (.i(i_8bit[5]), .s(s), .o(o_8bit[5]));
  memoria_1bit memoria_1bit_7 (.i(i_8bit[6]), .s(s), .o(o_8bit[6]));
  memoria_1bit memoria_1bit_8 (.i(i_8bit[7]), .s(s), .o(o_8bit[7]));
endmodule

module registrador_set_enable (
  input  [7:0] in_1,
  input  s,
  input  e,
  output [7:0] out_4
);

  wire [7:0] enable_1_out_3, memoria_8bit_1_o_8bit;

  memoria_8bit memoria_8bit_1 (.i_8bit(in_1), .s(s), .o_8bit(memoria_8bit_1_o_8bit));
  enable enable_1 (.in_1(memoria_8bit_1_o_8bit), .e(e), .out_3(enable_1_out_3));
  assign out_4 = e ? enable_1_out_3 : 8'bz;  // Controlled_Buffer controlled_buffer_1
endmodule

module deco_2x4 (
  input  in_1,
  input  in_2,
  output out_3,
  output out_4,
  output out_5,
  output out_6
);

  wire not_1_out, not_2_out;

  not not_1 (not_1_out, in_2);
  not not_2 (not_2_out, in_1);
  and and_1 (out_3, not_2_out, not_1_out);
  and and_2 (out_4, not_2_out, in_2);
  and and_3 (out_5, in_1, not_1_out);
  and and_4 (out_6, in_1, in_2);
endmodule

module memoria_256 (
  input  we,
  input  oe,
  input  [7:0] in_3,
  input  [7:0] in_4,
  output [7:0] out_5
);

  wire and_1_out, and_2_out, and_3_out, decoder_1_out0, decoder_1_out1, decoder_1_out2, decoder_1_out3,
       decoder_1_out4, decoder_1_out5, decoder_1_out6, decoder_1_out7, decoder_1_out8, decoder_1_out9,
       decoder_1_out10, decoder_1_out11, decoder_1_out12, decoder_1_out13, decoder_1_out14, decoder_1_out15,
       decoder_2_out0, decoder_2_out1, decoder_2_out2, decoder_2_out3, decoder_2_out4, decoder_2_out5,
       decoder_2_out6, decoder_2_out7, decoder_2_out8, decoder_2_out9, decoder_2_out10, decoder_2_out11,
       decoder_2_out12, decoder_2_out13, decoder_2_out14, decoder_2_out15;

  Decoder #(.select(4)) decoder_1 (
    .out0(decoder_1_out0), .out1(decoder_1_out1), .out2(decoder_1_out2), .out3(decoder_1_out3),
    .out4(decoder_1_out4), .out5(decoder_1_out5), .out6(decoder_1_out6), .out7(decoder_1_out7),
    .out8(decoder_1_out8), .out9(decoder_1_out9), .out10(decoder_1_out10), .out11(decoder_1_out11),
    .out12(decoder_1_out12), .out13(decoder_1_out13), .out14(decoder_1_out14), .out15(decoder_1_out15),
    .sel(in_3[7:4]));  // open: en
  Decoder #(.select(4)) decoder_2 (
    .out0(decoder_2_out0), .out1(decoder_2_out1), .out2(decoder_2_out2), .out3(decoder_2_out3),
    .out4(decoder_2_out4), .out5(decoder_2_out5), .out6(decoder_2_out6), .out7(decoder_2_out7),
    .out8(decoder_2_out8), .out9(decoder_2_out9), .out10(decoder_2_out10), .out11(decoder_2_out11),
    .out12(decoder_2_out12), .out13(decoder_2_out13), .out14(decoder_2_out14), .out15(decoder_2_out15),
    .sel(in_3[3:0]));  // open: en
  and and_1 (and_1_out, decoder_1_out0, decoder_2_out0);
  and and_2 (and_2_out, and_1_out, we);
  and and_3 (and_3_out, and_1_out, oe);
  registrador_set_enable registrador_set_enable_1 (.in_1(in_4), .s(and_2_out), .e(and_3_out), .out_4(out_5));
endmodule

module SHL (
  input  c_in,
  input  [15:0] in_2,
  output [15:0] out_3,
  output c_out
);


  assign c_out = in_2[15];
  assign out_3 = {in_2[14:0], c_in};
endmodule

module SHR (
  input  c_in,
  input  [15:0] in_2,
  output [15:0] out_3,
  output c_out
);


  assign c_out = in_2[0];
  assign out_3 = {c_in, in_2[15:1]};
endmodule

// ula
module ULA (
  input  [2:0] in_1,
  input  [15:0] A,
  input  [15:0] B,
  output carry_out,
  output [15:0] out_5,
  output A_larger_than_B,
  output A_equal_B,
  output zero
);

  wire adder_c_out, SL_c_out, SR_c_out;
  wire [15:0] adder_s_16bit, and_1_out, not_1_out, or_1_out, SL_out_3, SR_out_3, xor_1_out;

  somador_16bit adder (.a_16bit(A), .b_16bit(B), .c_in(1'b0), .c_out(adder_c_out), .s_16bit(adder_s_16bit));
  SHR SR (.in_2(A), .c_in(1'b0), .c_out(SR_c_out), .out_3(SR_out_3));
  SHL SL (.in_2(A), .c_in(1'b0), .c_out(SL_c_out), .out_3(SL_out_3));
  assign not_1_out = ~A;  // NOT_Gate not_1, 16 bits wide
  assign and_1_out = A & B;  // AND_Gate and_1, 16 bits wide
  assign or_1_out = A | B;  // OR_Gate or_1, 16 bits wide
  assign xor_1_out = A ^ B;  // XOR_Gate xor_1, 16 bits wide
  Comparator #(.width(16)) comparator_1 (.a(A), .b(B), .gt(A_larger_than_B), .eq(A_equal_B));  // open: lt
  Multiplexer #(.select(3)) multiplexer_1 (
    .in0(adder_c_out), .in1(SR_c_out), .in2(SL_c_out), .in3(1'b0), .in4(1'b0), .in5(1'b0), .in6(1'b0),
    .in7(1'b0), .out(carry_out), .sel(in_1));
  Multiplexer #(.select(3), .width(16)) multiplexer_2 (
    .in0(adder_s_16bit), .in1(SR_out_3), .in2(SL_out_3), .in3(not_1_out), .in4(and_1_out), .in5(or_1_out),
    .in6(xor_1_out), .in7(A), .out(out_5), .sel(in_1));
  nor nor_1 (zero, out_5[0], out_5[1], out_5[2], out_5[3], out_5[4], out_5[5], out_5[6], out_5[7], out_5[8], out_5[9], out_5[10], out_5[11], out_5[12], out_5[13], out_5[14], out_5[15]);
endmodule

module clk (
  output set,
  output enable
);

  wire clk_1_out, not_1_out, t_ff_1_q;

  Clock clk_1 (.out(clk_1_out));
  T_Flip_Flop t_ff_1 (.clk(clk_1_out), .T(1'b1), .Q(t_ff_1_q));  // open: Qn, preset, reset
  not not_1 (not_1_out, clk_1_out);
  and and_1 (set, not_1_out, t_ff_1_q);
  or or_1 (enable, t_ff_1_q, clk_1_out);
endmodule

module stepper (
  input  clk_2,
  output init,
  output s1,
  output s2,
  output s3,
  output s4,
  output s5,
  output s6
);

  wire decoder_1_out7;
  wire [2:0] counter_1_q;

  Counter #(.max('h7), .width(3)) counter_1 (
    .D(3'b000), .Q(counter_1_q), .clk(clk_2), .clr(decoder_1_out7));  // open: load, count, carry, up
  Decoder #(.enable("false"), .select(3)) decoder_1 (
    .out0(init), .out1(s1), .out2(s2), .out3(s3), .out4(s4), .out5(s5), .out6(s6), .out7(decoder_1_out7),
    .sel(counter_1_q));
endmodule

module bus_1 (
  input  [15:0] i,
  input  s,
  output [15:0] o
);

  Multiplexer #(.width(16)) multiplexer_1 (.in0(i), .in1(16'h1), .out(o), .sel(s));
endmodule

module UC (
  input  in_1,
  input  in_2,
  input  in_3,
  input  in_4,
  input  [15:0] in_5,
  output out_6,
  output out_7,
  output out_8,
  output out_9,
  output out_10,
  output out_11,
  output out_12,
  output out_13,
  output out_14,
  output out_15,
  output [2:0] out_16,
  output out_17,
  output out_18,
  output out_19,
  output out_20,
  output out_21,
  output out_22,
  output out_23,
  output out_24,
  output out_25,
  output out_26,
  output out_27,
  output out_28,
  output out_29,
  output out_30
);

  wire a_out, and_5_out, and_6_out, and_7_out, and_8_out, and_9_out, and_10_out, and_11_out, and_12_out,
       and_16_out, and_17_out, and_18_out, and_19_out, and_20_out, and_21_out, and_22_out, and_23_out,
       and_24_out, and_25_out, and_26_out, and_27_out, and_28_out, and_29_out, and_30_out, and_31_out,
       and_32_out, and_33_out, and_34_out, and_35_out, and_36_out, and_37_out, and_38_out, and_39_out,
       and_40_out, and_41_out, and_42_out, and_43_out, c_out, clk_s_e_enable, clk_s_e_set, decoder_1_out0,
       decoder_1_out1, decoder_1_out2, decoder_1_out3, decoder_2_out0, decoder_2_out1, decoder_2_out2,
       decoder_2_out3, decoder_3_out0, decoder_3_out1, decoder_3_out2, decoder_3_out3, decoder_3_out4,
       decoder_3_out5, decoder_3_out6, decoder_3_out7, decoder_4_out0, decoder_4_out1, decoder_4_out2,
       decoder_4_out3, e_out, not_1_out, not_2_out, not_3_out, or_6_out, or_7_out, or_8_out, or_9_out,
       or_10_out, or_11_out, or_12_out, or_13_out, ra_e_out, rb_e_out, rb_s_out, stepper_1_s1, stepper_1_s2,
       stepper_1_s3, stepper_1_s4, stepper_1_s5, stepper_1_s6, z_out;

  or or_1 (out_9, and_5_out, and_9_out);
  or or_2 (out_11, and_6_out, and_10_out);
  or or_3 (out_13, and_7_out, and_11_out);
  or or_4 (out_15, and_8_out, and_12_out);
  and and_1 (out_27, clk_s_e_enable, or_6_out);
  and and_2 (out_19, clk_s_e_enable, or_7_out);
  and and_3 (out_22, clk_s_e_enable, or_8_out);
  and and_4 (out_28, clk_s_e_enable, and_40_out);
  and and_5 (and_5_out, clk_s_e_enable, rb_e_out, decoder_1_out0);
  and and_6 (and_6_out, clk_s_e_enable, rb_e_out, decoder_1_out1);
  and and_7 (and_7_out, clk_s_e_enable, rb_e_out, decoder_1_out2);
  and and_8 (and_8_out, clk_s_e_enable, rb_e_out, decoder_1_out3);
  and and_9 (and_9_out, clk_s_e_enable, ra_e_out, decoder_2_out0);
  and and_10 (and_10_out, clk_s_e_enable, ra_e_out, decoder_2_out1);
  and and_11 (and_11_out, clk_s_e_enable, ra_e_out, decoder_2_out2);
  and and_12 (and_12_out, clk_s_e_enable, ra_e_out, decoder_2_out3);
  clk clk_s_e (.set(clk_s_e_set), .enable(clk_s_e_enable));
  or or_5 (out_7, stepper_1_s1, and_31_out, and_30_out, and_27_out);
  or or_6 (or_6_out, stepper_1_s1, and_27_out, and_29_out, and_30_out);
  or or_7 (or_7_out, stepper_1_s2, and_43_out, and_38_out, and_37_out, and_35_out);
  or or_8 (or_8_out, stepper_1_s3, and_39_out, and_42_out, and_41_out);
  or rb_e (rb_e_out, and_24_out, and_36_out, and_28_out, and_32_out);
  or ra_e (ra_e_out, and_26_out, and_25_out, and_34_out);
  Decoder #(.enable("false"), .select(2)) decoder_1 (
    .out0(decoder_1_out0), .out1(decoder_1_out1), .out2(decoder_1_out2), .out3(decoder_1_out3),
    .sel(in_5[1:0]));
  Decoder #(.enable("false"), .select(2)) decoder_2 (
    .out0(decoder_2_out0), .out1(decoder_2_out1), .out2(decoder_2_out2), .out3(decoder_2_out3),
    .sel(in_5[3:2]));
  and and_13 (out_16[0], stepper_1_s5, in_5[15], in_5[12]);
  and and_14 (out_16[1], stepper_1_s5, in_5[15], in_5[13]);
  and and_15 (out_16[2], stepper_1_s5, in_5[15], in_5[14]);
  stepper stepper_1 (
    .clk_2(clk_s_e_enable), .init(out_20), .s1(stepper_1_s1), .s2(stepper_1_s2), .s3(stepper_1_s3),
    .s4(stepper_1_s4), .s5(stepper_1_s5), .s6(stepper_1_s6));
  not not_1 (not_1_out, in_5[15]);
  Decoder #(.enable("false"), .select(3)) decoder_3 (
    .out0(decoder_3_out0), .out1(decoder_3_out1), .out2(decoder_3_out2), .out3(decoder_3_out3),
    .out4(decoder_3_out4), .out5(decoder_3_out5), .out6(decoder_3_out6), .out7(decoder_3_out7),
    .sel(in_5[14:12]));
  and and_16 (and_16_out, not_1_out, decoder_3_out0);
  and and_17 (and_17_out, not_1_out, decoder_3_out1);
  and and_18 (and_18_out, not_1_out, decoder_3_out2);
  and and_19 (and_19_out, not_1_out, decoder_3_out3);
  and and_20 (and_20_out, not_1_out, decoder_3_out4);
  and and_21 (and_21_out, not_1_out, decoder_3_out5);
  and and_22 (and_22_out, not_1_out, decoder_3_out6);
  and and_23 (and_23_out, not_1_out, decoder_3_out7);
  and c (c_out, in_5[3], in_1);
  and a (a_out, in_5[2], in_2);
  and e (e_out, in_5[1], in_3);
  and z (z_out, in_5[0], in_4);
  and and_24 (and_24_out, stepper_1_s4, in_5[15]);
  and and_25 (and_25_out, stepper_1_s4, and_16_out);
  and and_26 (and_26_out, stepper_1_s4, and_17_out);
  and and_27 (and_27_out, stepper_1_s4, and_18_out);
  and and_28 (and_28_out, stepper_1_s4, and_19_out);
  and and_29 (and_29_out, stepper_1_s4, and_20_out);
  and and_30 (and_30_out, stepper_1_s4, and_21_out);
  and and_31 (and_31_out, stepper_1_s4, and_22_out);
  and and_32 (and_32_out, stepper_1_s4, and_23_out, in_5[3]);
  or or_9 (or_9_out, c_out, a_out, e_out, z_out);
  not not_2 (not_2_out, in_5[3]);
  and and_33 (and_33_out, in_5[12], in_5[13], in_5[14]);
  not not_3 (not_3_out, and_33_out);
  and and_34 (and_34_out, stepper_1_s5, in_5[15]);
  and and_35 (and_35_out, stepper_1_s5, and_16_out);
  and and_36 (and_36_out, stepper_1_s5, and_17_out);
  and and_37 (and_37_out, stepper_1_s5, and_18_out);
  and and_38 (and_38_out, stepper_1_s5, and_20_out);
  and and_39 (and_39_out, stepper_1_s5, and_21_out);
  and and_40 (and_40_out, stepper_1_s5, and_23_out, not_2_out);
  and and_41 (and_41_out, stepper_1_s6, in_5[15], not_3_out);
  and and_42 (and_42_out, stepper_1_s6, and_18_out);
  and and_43 (and_43_out, stepper_1_s6, and_21_out, or_9_out);
  Decoder #(.enable("false"), .select(2)) decoder_4 (
    .out0(decoder_4_out0), .out1(decoder_4_out1), .out2(decoder_4_out2), .out3(decoder_4_out3),
    .sel(in_5[1:0]));
  or or_10 (or_10_out, stepper_1_s1, and_27_out, and_30_out, and_25_out, and_26_out, and_29_out);
  or or_11 (or_11_out, stepper_1_s3, and_28_out, and_38_out, and_39_out, and_42_out, and_43_out);
  or or_12 (or_12_out, stepper_1_s1, and_27_out, and_30_out, and_34_out);
  or or_13 (or_13_out, and_31_out, and_34_out);
  or rb_s (rb_s_out, and_35_out, and_41_out, and_37_out, and_40_out);
  and and_44 (out_30, clk_s_e_set, stepper_1_s2);
  and and_45 (out_17, clk_s_e_set, or_10_out);
  and and_46 (out_26, clk_s_e_set, or_11_out);
  and and_47 (out_25, clk_s_e_set, or_12_out);
  and and_48 (out_18, clk_s_e_set, and_36_out);
  and and_49 (out_6, clk_s_e_set, and_24_out);
  and and_50 (out_21, clk_s_e_set, or_13_out);
  and and_51 (out_29, clk_s_e_set, and_32_out);
  and and_52 (out_8, clk_s_e_set, rb_s_out, decoder_4_out0);
  and and_53 (out_10, clk_s_e_set, rb_s_out, decoder_4_out1);
  and and_54 (out_12, clk_s_e_set, rb_s_out, decoder_4_out2);
  and and_55 (out_14, clk_s_e_set, rb_s_out, decoder_4_out3);

  assign out_23 = in_5[3];
  assign out_24 = in_5[2];

  // Other names for the same wires on the sheet: from_ir[15:0] = in_5; data_address = in_5[2]; input_output = in_5[3];
  //   from_c_out = in_1; from_equal = in_3; from_larger = in_2; from_zero = in_4; init = out_20; R0_e = out_9;
  //   R0_s = out_8; R1_e = out_11; R1_s = out_10; R2_e = out_13; R2_s = out_12; R3_e = out_15; R3_s = out_14;
  //   to_acc_e = out_22; to_acc_s = out_25; to_bus_1 = out_7; to_flag_s = out_21; to_iar_e = out_27;
  //   to_iar_s = out_26; to_io_clk_e = out_28; to_io_clk_s = out_29; to_ir_s = out_30; to_mar_s = out_17;
  //   to_ram_e = out_19; to_ram_s = out_18; to_tmp_s = out_6; to_ula[2:0] = out_16
endmodule

module flag (
  input  in_1,
  input  in_2,
  input  in_3,
  input  in_4,
  input  in_5,
  output out_6,
  output out_7,
  output out_8,
  output out_9
);

  Register #(.width(4)) register_1 (
    .D({in_4, in_3, in_2, in_1}), .Q({out_9, out_8, out_7, out_6}), .clk(in_5));  // open: en, clr
endmodule

module teclado (
  input  [15:0] in_1,
  input  in_2,
  input  [6:0] in_3,
  input  in_4,
  input  in_5,
  input  in_6,
  output [15:0] out_7,
  output out_8,
  output out_9
);

  wire and_1_out, comparator_1_eq;
  wire [15:0] bit_extender_1_out;

  Comparator #(.width(16)) comparator_1 (.a(in_1), .b({16{1'b0}}), .eq(comparator_1_eq));  // open: gt, lt
  and and_1 (and_1_out, in_4, in_5, in_6);
  T_Flip_Flop t_ff_1 (.clk(in_2), .T(1'b1), .Qn(out_8));  // open: Q, preset, reset
  Register #(.width(1)) register_1 (.D(comparator_1_eq), .Q(out_9), .clk(and_1_out));  // open: en, clr
  assign out_7 = in_2 ? bit_extender_1_out : 16'bz;  // Controlled_Buffer controlled_buffer_1
  assign bit_extender_1_out = {{9{1'b0}}, in_3};  // Bit_Extender bit_extender_1
endmodule

module monitor_adaptador (
  input  [15:0] in_1,
  input  io,
  input  da,
  input  ios,
  output [6:0] out_5,
  output to_ms,
  output to_m
);

  wire and_1_out, comparator_1_eq;

  Bit_Extender #(.in_width(16), .out_width(7), .\type ("zero")) bit_extender_1 (.in(in_1), .out(out_5));
  Comparator #(.width(16)) comparator_1 (.a(in_1), .b(16'h1), .eq(comparator_1_eq));  // open: gt, lt
  Register #(.width(1)) register_1 (.D(comparator_1_eq), .Q(to_m), .clk(and_1_out));  // open: en, clr
  and and_1 (and_1_out, io, da, ios);

  assign to_ms = ios;
endmodule

module adaptador_porta (
  input  [15:0] in_1,
  input  io,
  input  da,
  input  ios,
  output to_ms,
  output to_m
);

  wire and_1_out, comparator_1_eq;

  Comparator #(.width(16)) comparator_1 (.a(in_1), .b(16'h2), .eq(comparator_1_eq));  // open: gt, lt
  Register #(.width(1)) register_1 (.D(comparator_1_eq), .Q(to_m), .clk(and_1_out));  // open: en, clr
  and and_1 (and_1_out, io, da, ios);

  assign to_ms = ios;
endmodule
