// Logisim project marcos_cpu_16bits.circ as structural Verilog: 25 circuits, main circuit main
module main (
);

  wire adapter_clear_buffer, adapter_clk_key, adapter_clk_port_p, adapter_clk_tty, adapter_key_on,
       adapter_port_p_on, adapter_tty_on, flag_1_a, flag_1_c, flag_1_e, flag_1_z, or_1_out, portio_1_p3,
       uc_1_acc_e, uc_1_acc_s, uc_1_bus1, uc_1_data_addr, uc_1_flag_s, uc_1_iar_e, uc_1_iar_s, uc_1_io,
       uc_1_io_clk_e, uc_1_io_clk_s, uc_1_ir_s, uc_1_mar_s, uc_1_r0_e, uc_1_r0_s, uc_1_r1_e, uc_1_r1_s,
       uc_1_r2_e, uc_1_r2_s, uc_1_r3_e, uc_1_r3_s, uc_1_ram_e, uc_1_ram_s, uc_1_tmp_s, ula_1_a_igual_b,
       ula_1_a_maior_b, ula_1_c_out, ula_1_zero;
  wire [2:0] uc_1_to_ula;
  wire [6:0] adapter_to_tty, keyboard_1_data, uc_1_step;
  wire [15:0] ACC_q, adapter_to_port_p, bus_1_1_out_3, controlled_buffer_1_out, controlled_buffer_7_out,
       IAR_q, IR_q, MAR_q, R0_q, R1_q, R2_q, R3_q, TMP_q, ula_1_saida;

  Register #(.width(16)) TMP (.D(controlled_buffer_1_out), .Q(TMP_q), .clk(uc_1_tmp_s));  // open: en, clr
  bus_1 bus_1_1 (.in_1(TMP_q), .out_3(bus_1_1_out_3), .in_2(uc_1_bus1));
  ULA ula_1 (
    .A(controlled_buffer_1_out), .B(bus_1_1_out_3), .saida(ula_1_saida), .seleciona(uc_1_to_ula),
    .c_out(ula_1_c_out), .A_maior_B(ula_1_a_maior_b), .A_igual_B(ula_1_a_igual_b), .zero(ula_1_zero));  // open: c_in
  Register #(.width(16)) ACC (.D(ula_1_saida), .Q(ACC_q), .clk(uc_1_acc_s));  // open: en, clr
  assign controlled_buffer_1_out = uc_1_r0_e ? R0_q : 16'bz;  // Controlled_Buffer controlled_buffer_1
  Register #(.width(16)) R0 (.D(controlled_buffer_1_out), .Q(R0_q), .clk(uc_1_r0_s));  // open: en, clr
  flag flag_1 (
    .in_1(ula_1_c_out), .in_2(ula_1_a_maior_b), .in_4(ula_1_a_igual_b), .in_5(ula_1_zero),
    .flag_s(uc_1_flag_s), .C(flag_1_c), .A(flag_1_a), .E(flag_1_e), .Z(flag_1_z));
  assign controlled_buffer_1_out = uc_1_acc_e ? ACC_q : 16'bz;  // Controlled_Buffer controlled_buffer_2
  Register #(.width(16)) R1 (.D(controlled_buffer_1_out), .Q(R1_q), .clk(uc_1_r1_s));  // open: en, clr
  assign controlled_buffer_1_out = uc_1_r1_e ? R1_q : 16'bz;  // Controlled_Buffer controlled_buffer_3
  assign controlled_buffer_1_out = uc_1_r2_e ? R2_q : 16'bz;  // Controlled_Buffer controlled_buffer_4
  Register #(.width(16)) R2 (.D(controlled_buffer_1_out), .Q(R2_q), .clk(uc_1_r2_s));  // open: en, clr
  UC uc_1 (
    .TMP_s(uc_1_tmp_s), .bus1(uc_1_bus1), .to_ula(uc_1_to_ula), .C(flag_1_c), .A(flag_1_a), .E(flag_1_e),
    .Z(flag_1_z), .R0_s(uc_1_r0_s), .R0_e(uc_1_r0_e), .R1_s(uc_1_r1_s), .R1_e(uc_1_r1_e), .R2_s(uc_1_r2_s),
    .R2_e(uc_1_r2_e), .R3_s(uc_1_r3_s), .R3_e(uc_1_r3_e), .FLAG_s(uc_1_flag_s), .ACC_e(uc_1_acc_e),
    .ACC_s(uc_1_acc_s), .IAR_s(uc_1_iar_s), .IAR_e(uc_1_iar_e), .IR(IR_q), .IR_s(uc_1_ir_s),
    .MAR_s(uc_1_mar_s), .RAM_s(uc_1_ram_s), .RAM_e(uc_1_ram_e), .step(uc_1_step), .IO_clk_e(uc_1_io_clk_e),
    .IO_clk_s(uc_1_io_clk_s), .DATA_ADDR(uc_1_data_addr), .IO(uc_1_io));
  Register #(.width(16)) R3 (.D(controlled_buffer_1_out), .Q(R3_q), .clk(uc_1_r3_s));  // open: en, clr
  Register #(.width(16)) IAR (.D(controlled_buffer_1_out), .Q(IAR_q), .clk(uc_1_iar_s));  // open: en, clr
  assign controlled_buffer_1_out = uc_1_iar_e ? IAR_q : 16'bz;  // Controlled_Buffer controlled_buffer_5
  // Probe on controlled_buffer_1_out
  assign controlled_buffer_1_out = uc_1_r3_e ? R3_q : 16'bz;  // Controlled_Buffer controlled_buffer_6
  DotMatrix #(.dotshape("clusterSegment"), .inputtype("row"), .matrixcols(7), .matrixrows(1)) steps (.row0(uc_1_step));
  Register #(.width(16)) IR (.D(controlled_buffer_1_out), .Q(IR_q), .clk(uc_1_ir_s));  // open: en, clr
  Register #(.width(16)) MAR (.D(controlled_buffer_1_out), .Q(MAR_q), .clk(uc_1_mar_s));  // open: en, clr
  or or_1 (or_1_out, uc_1_ram_s, uc_1_ram_e);
  adaptador adapter (
    .IO_e(uc_1_io_clk_e), .IO_s(uc_1_io_clk_s), .D_A(uc_1_data_addr), .I_O(uc_1_io),
    .from_bus(controlled_buffer_1_out), .to_bus(controlled_buffer_1_out), .to_tty(adapter_to_tty),
    .clk_tty(adapter_clk_tty), .tty_on(adapter_tty_on), .clear_buffer(adapter_clear_buffer),
    .clk_key(adapter_clk_key), .key_on(adapter_key_on), .from_key(keyboard_1_data),
    .to_port_p(adapter_to_port_p), .clk_port_p(adapter_clk_port_p), .port_p_on(adapter_port_p_on));
  RAM #(.addrWidth(16), .dataWidth(16), .databus("bidir"), .\type ("nonvolatile")) RAM_256 (
    .addr(MAR_q), .we(uc_1_ram_s), .oe(uc_1_ram_e), .clk(or_1_out));  // open: data
  TTY tty_1 (.data(adapter_to_tty), .clk(adapter_clk_tty), .we(adapter_tty_on), .clr(adapter_clear_buffer));
  Keyboard keyboard_1 (
    .clk(adapter_clk_key), .re(adapter_key_on), .clr(adapter_clear_buffer), .data(keyboard_1_data));  // open: avail
  // Probe on portio_1_p3
  assign controlled_buffer_7_out = adapter_clk_port_p ? adapter_to_port_p : 16'bz;  // Controlled_Buffer controlled_buffer_7
  // PortIO #(.number(16)) portio_1: pin names not known; wires that end beside it: adapter_port_p_on, controlled_buffer_7_out, portio_1_p3

  // Notes on the sheet:
  //   Marcos Paulo Vieira Pedrosa - 22401906
endmodule

module meio_somador (
  input  c_in,
  input  a,
  output c_out,
  output o
);

  and and_1 (c_out, c_in, a);
  xor xor_1 (o, c_in, a);
endmodule

module somador_completo_1bit (
  input  c_in,
  input  a,
  input  b,
  output o,
  output c_out
);

  wire and_1_out, and_2_out, xor_1_out;

  and and_1 (and_1_out, a, b);
  xor xor_1 (xor_1_out, a, b);
  and and_2 (and_2_out, c_in, xor_1_out);
  xor xor_2 (o, xor_1_out, c_in);
  or or_1 (c_out, and_1_out, and_2_out);
endmodule

module somador_8bits (
  input  c_in,
  input  [7:0] a_8bit,
  input  [7:0] b_8bit,
  output [7:0] o_8bit,
  output c_out
);

  wire somador_completo_1bit_1_c_out, somador_completo_1bit_2_c_out, somador_completo_1bit_3_c_out,
       somador_completo_1bit_4_c_out, somador_completo_1bit_5_c_out, somador_completo_1bit_6_c_out,
       somador_completo_1bit_7_c_out;

  somador_completo_1bit somador_completo_1bit_1 (
    .a(a_8bit[0]), .b(b_8bit[0]), .c_in(c_in), .c_out(somador_completo_1bit_1_c_out), .o(o_8bit[0]));
  somador_completo_1bit somador_completo_1bit_2 (
    .a(a_8bit[1]), .b(b_8bit[1]), .c_in(somador_completo_1bit_1_c_out),
    .c_out(somador_completo_1bit_2_c_out), .o(o_8bit[1]));
  somador_completo_1bit somador_completo_1bit_3 (
    .a(a_8bit[2]), .b(b_8bit[2]), .c_in(somador_completo_1bit_2_c_out),
    .c_out(somador_completo_1bit_3_c_out), .o(o_8bit[2]));
  somador_completo_1bit somador_completo_1bit_4 (
    .a(a_8bit[3]), .b(b_8bit[3]), .c_in(somador_completo_1bit_3_c_out),
    .c_out(somador_completo_1bit_4_c_out), .o(o_8bit[3]));
  somador_completo_1bit somador_completo_1bit_5 (
    .a(a_8bit[4]), .b(b_8bit[4]), .c_in(somador_completo_1bit_4_c_out),
    .c_out(somador_completo_1bit_5_c_out), .o(o_8bit[4]));
  somador_completo_1bit somador_completo_1bit_6 (
    .a(a_8bit[5]), .b(b_8bit[5]), .c_in(somador_completo_1bit_5_c_out),
    .c_out(somador_completo_1bit_6_c_out), .o(o_8bit[5]));
  somador_completo_1bit somador_completo_1bit_7 (
    .a(a_8bit[6]), .b(b_8bit[6]), .c_in(somador_completo_1bit_6_c_out),
    .c_out(somador_completo_1bit_7_c_out), .o(o_8bit[6]));
  somador_completo_1bit somador_completo_1bit_8 (
    .a(a_8bit[7]), .b(b_8bit[7]), .c_in(somador_completo_1bit_7_c_out), .c_out(c_out), .o(o_8bit[7]));
endmodule

module memoria_1bit (
  input  i,
  input  set,
  output o
);

  wire nand_1_out, nand_2_out, nand_4_out;

  nand nand_1 (nand_1_out, i, set);
  nand nand_2 (nand_2_out, nand_1_out, set);
  nand nand_3 (o, nand_1_out, nand_4_out);
  nand nand_4 (nand_4_out, o, nand_2_out);
endmodule

module memoria_8bits (
  input  [7:0] i_8bit,
  input  set,
  output [7:0] o_8bit
);

  memoria_1bit memoria_1bit_1 (.i(i_8bit[0]), .set(set), .o(o_8bit[0]));
  memoria_1bit memoria_1bit_2 (.i(i_8bit[1]), .set(set), .o(o_8bit[1]));
  memoria_1bit memoria_1bit_3 (.i(i_8bit[2]), .set(set), .o(o_8bit[2]));
  memoria_1bit memoria_1bit_4 (.i(i_8bit[3]), .set(set), .o(o_8bit[3]));
  memoria_1bit memoria_1bit_5 (.i(i_8bit[4]), .set(set), .o(o_8bit[4]));
  memoria_1bit memoria_1bit_6 (.i(i_8bit[5]), .set(set), .o(o_8bit[5]));
  memoria_1bit memoria_1bit_7 (.i(i_8bit[6]), .set(set), .o(o_8bit[6]));
  memoria_1bit memoria_1bit_8 (.i(i_8bit[7]), .set(set), .o(o_8bit[7]));
endmodule

module enabler (
  input  [7:0] i_8bit,
  input  e,
  output [7:0] o_8bit
);

  and and_1 (o_8bit[0], i_8bit[0], e);
  and and_2 (o_8bit[1], i_8bit[1], e);
  and and_3 (o_8bit[2], i_8bit[2], e);
  and and_4 (o_8bit[3], i_8bit[3], e);
  and and_5 (o_8bit[4], i_8bit[4], e);
  and and_6 (o_8bit[5], i_8bit[5], e);
  and and_7 (o_8bit[6], i_8bit[6], e);
  and and_8 (o_8bit[7], i_8bit[7], e);
endmodule

module registrador_8bits (
  input  [7:0] i_8bit,
  input  s,
  input  e,
  output [7:0] o_8bit
);

  wire [7:0] memoria_8bits_1_o_8bit;

  memoria_8bits memoria_8bits_1 (.i_8bit(i_8bit), .set(s), .o_8bit(memoria_8bits_1_o_8bit));
  enabler enabler_1 (.i_8bit(memoria_8bits_1_o_8bit), .e(e), .o_8bit(o_8bit));
endmodule

module registrador_8bits_buffer (
  input  [7:0] i_8bit,
  input  s,
  input  e,
  output [7:0] o_8bit
);

  wire [7:0] registrador_8bits_1_o_8bit;

  assign o_8bit = e ? registrador_8bits_1_o_8bit : 8'bz;  // Controlled_Buffer controlled_buffer_1
  registrador_8bits registrador_8bits_1 (.i_8bit(i_8bit), .s(s), .e(e), .o_8bit(registrador_8bits_1_o_8bit));
endmodule

// 2-4
module decoder_2x4 (
  input  in_1,
  input  in_2,
  output out_3,
  output out_4,
  output out_5,
  output out_6
);

  wire not_1_out, not_2_out;

  not not_1 (not_1_out, in_1);
  not not_2 (not_2_out, in_2);
  and and_1 (out_3, not_1_out, not_2_out);
  and and_2 (out_4, in_1, not_2_out);
  and and_3 (out_5, not_1_out, in_2);
  and and_4 (out_6, in_1, in_2);
endmodule

module memoria_256 (
  input  [7:0] in_1,
  input  we,
  input  oe,
  output out_4
);

  Decoder #(.enable("false"), .select(4)) decoder_1 (.sel(in_1[7:4]));  // open: out0, out1, out2, out3, out4, out5, out6, out7, out8, out9, out10, out11, out12, out13, out14, out15
  Decoder #(.enable("false"), .select(4)) decoder_2 (.sel(in_1[3:0]));  // open: out0, out1, out2, out3, out4, out5, out6, out7, out8, out9, out10, out11, out12, out13, out14, out15

  assign out_4 = we;
endmodule

module SHR (
  input  c_in,
  input  [15:0] in_2,
  output [15:0] out_3,
  output c_out
);


  assign c_out = in_2[0];
  assign out_3 = {c_in, in_2[15:1]};
endmodule

module SHL (
  input  c_in,
  input  [15:0] in_2,
  output [15:0] out_3,
  output c_out
);


  assign c_out = in_2[15];
  assign out_3 = {in_2[14:0], c_in};
endmodule

module ULA (
  input  [2:0] seleciona,
  input  c_in,
  input  [15:0] A,
  input  [15:0] B,
  output c_out,
  output [15:0] saida,
  output A_maior_B,
  output A_igual_B,
  output zero
);

  wire SL_c_out, somador_16bits_1_c_out, SR_c_out;
  wire [15:0] and_1_out, not_1_out, or_1_out, SL_out_3, somador_16bits_1_o_16bit, SR_out_3, xor_1_out;

  somador_16bits somador_16bits_1 (
    .a_16bit(B), .b_16bit(A), .c_in(c_in), .c_out(somador_16bits_1_c_out), .o_16bit(somador_16bits_1_o_16bit));
  SHR SR (.in_2(A), .c_in(c_in), .c_out(SR_c_out), .out_3(SR_out_3));
  SHL SL (.in_2(A), .c_in(c_in), .c_out(SL_c_out), .out_3(SL_out_3));
  assign not_1_out = ~A;  // NOT_Gate not_1, 16 bits wide
  Comparator #(.width(16)) comparator_1 (.a(A), .b(B), .gt(A_maior_B), .eq(A_igual_B));  // open: lt
  assign and_1_out = B & A;  // AND_Gate and_1, 16 bits wide
  assign or_1_out = B | A;  // OR_Gate or_1, 16 bits wide
  assign xor_1_out = B ^ A;  // XOR_Gate xor_1, 16 bits wide
  Multiplexer #(.select(3)) multiplexer_1 (
    .in0(somador_16bits_1_c_out), .in1(SR_c_out), .in2(SL_c_out), .in3(1'b0), .in4(1'b0), .in5(1'b0),
    .in6(1'b0), .in7(1'b0), .out(c_out), .sel(seleciona));
  Multiplexer #(.select(3), .width(16)) multiplexer_2 (
    .in0(somador_16bits_1_o_16bit), .in1(SR_out_3), .in2(SL_out_3), .in3(not_1_out), .in4(and_1_out),
    .in5(or_1_out), .in6(xor_1_out), .in7(A), .out(saida), .sel(seleciona));
  nor nor_1 (zero, saida[0], saida[1], saida[2], saida[3], saida[4], saida[5], saida[6], saida[7], saida[8], saida[9], saida[10], saida[11], saida[12], saida[13], saida[14], saida[15]);
endmodule

// Stepper
module stepper (
  input  clk,
  output init,
  output s1,
  output s2,
  output s3,
  output s4,
  output s5,
  output s6
);

  wire decoder_1_out7;
  wire [2:0] counter_1_q;

  Counter #(.max('h7), .width(3)) counter_1 (
    .D(3'b000), .Q(counter_1_q), .clk(clk), .clr(decoder_1_out7));  // open: load, count, carry, up
  Decoder #(.enable("false"), .select(3)) decoder_1 (
    .out0(init), .out1(s1), .out2(s2), .out3(s3), .out4(s4), .out5(s5), .out6(s6), .out7(decoder_1_out7),
    .sel(counter_1_q));
endmodule

module clk (
  output clk_e,
  output clk_s
);

  wire clk_out, not_1_out, t_ff_1_q;

  Clock clk (.out(clk_out));
  not not_1 (not_1_out, clk_out);
  T_Flip_Flop t_ff_1 (.clk(clk_out), .T(1'b1), .Q(t_ff_1_q));  // open: Qn, preset, reset
  and and_1 (clk_s, not_1_out, t_ff_1_q);
  or or_1 (clk_e, t_ff_1_q, clk_out);
endmodule

module clk_alternativo (
  output out_1,
  output out_2,
  output clk_e,
  output clk_s
);

  Clock #(.highDuration(2), .lowDuration(2)) clk1 (.out(out_1));
  Clock #(.highDuration(2), .lowDuration(2), .phaseOffset(1)) clk2 (.out(out_2));
  or or_1 (clk_e, out_2, out_1);
  and and_1 (clk_s, out_2, out_1);
endmodule

// b1
module bus_1 (
  input  [15:0] in_1,
  input  in_2,
  output [15:0] out_3
);

  Multiplexer #(.width(16)) multiplexer_1 (.in0(in_1), .in1(16'h1), .out(out_3), .sel(in_2));
endmodule

module UC (
  input  C,
  input  A,
  input  E,
  input  Z,
  input  [15:0] IR,
  output R0_s,
  output R0_e,
  output R1_s,
  output R1_e,
  output R2_s,
  output R2_e,
  output R3_s,
  output R3_e,
  output TMP_s,
  output MAR_s,
  output bus1,
  output RAM_s,
  output [2:0] to_ula,
  output RAM_e,
  output [6:0] step,
  output IO_clk_e,
  output IO_clk_s,
  output DATA_ADDR,
  output IO,
  output FLAG_s,
  output ACC_e,
  output ACC_s,
  output IAR_s,
  output IAR_e,
  output IR_s
);

  wire and_5_out, and_6_out, and_7_out, and_8_out, and_9_out, and_10_out, and_11_out, and_12_out, and_13_out,
       and_14_out, and_15_out, and_16_out, and_17_out, and_18_out, and_19_out, and_20_out, and_21_out,
       and_22_out, and_23_out, and_24_out, and_25_out, and_26_out, and_27_out, and_28_out, and_29_out,
       and_30_out, and_31_out, and_32_out, and_33_out, and_45_out, and_46_out, and_47_out, and_48_out,
       and_49_out, and_50_out, and_51_out, and_52_out, and_53_out, and_54_out, and_55_out, and_56_out,
       and_57_out, and_58_out, and_59_out, and_60_out, and_61_out, and_62_out, and_63_out, and_64_out,
       and_65_out, and_66_out, and_67_out, and_68_out, and_69_out, and_70_out, and_71_out, CAEZ, CLF,
       clk_1_clk_e, clk_1_clk_s, DATA, decoder_1_out0, decoder_1_out1, decoder_1_out2, decoder_1_out3,
       decoder_2_out0, decoder_2_out1, decoder_2_out2, decoder_2_out3, decoder_4_out0, decoder_4_out1,
       decoder_4_out2, decoder_4_out3, IN_OUT, JCAEZ, JMP, JMPR, LD, not_1_out, not_2_out, not_3_out,
       NOT_CMP, or_7_out, or_8_out, or_10_out, or_12_out, or_14_out, or_15_out, or_16_out, Reg_A_e, Reg_B_e,
       Reg_B_s, ST;
  wire [7:0] decoder_3_out0;

  or or_1 (R0_e, and_5_out, and_9_out);
  or or_2 (R1_e, and_6_out, and_10_out);
  or or_3 (R2_e, and_7_out, and_11_out);
  or or_4 (R3_e, and_8_out, and_12_out);
  and and_1 (ACC_e, or_7_out, clk_1_clk_e);
  and and_2 (RAM_e, or_8_out, clk_1_clk_e);
  and and_3 (IAR_e, or_10_out, clk_1_clk_e);
  and and_4 (IO_clk_e, and_13_out, clk_1_clk_e);
  and and_5 (and_5_out, clk_1_clk_e, Reg_B_e, decoder_1_out0);
  and and_6 (and_6_out, clk_1_clk_e, Reg_B_e, decoder_1_out1);
  and and_7 (and_7_out, clk_1_clk_e, Reg_B_e, decoder_1_out2);
  and and_8 (and_8_out, clk_1_clk_e, Reg_B_e, decoder_1_out3);
  and and_9 (and_9_out, clk_1_clk_e, Reg_A_e, decoder_2_out0);
  and and_10 (and_10_out, clk_1_clk_e, Reg_A_e, decoder_2_out1);
  and and_11 (and_11_out, clk_1_clk_e, Reg_A_e, decoder_2_out2);
  and and_12 (and_12_out, clk_1_clk_e, Reg_A_e, decoder_2_out3);
  or or_5 (Reg_B_e, and_14_out, and_15_out, and_16_out, and_17_out);
  or or_6 (Reg_A_e, and_18_out, and_19_out, and_20_out);
  or or_7 (or_7_out, and_21_out, and_22_out, and_23_out, step[3]);
  or or_8 (or_8_out, and_24_out, and_25_out, and_26_out, and_27_out, step[2]);
  or or_9 (bus1, and_28_out, and_29_out, and_30_out, step[1]);
  or or_10 (or_10_out, and_31_out, and_32_out, and_33_out, step[1]);
  and and_13 (and_13_out, step[5], IN_OUT, not_1_out);
  Decoder #(.enable("false"), .select(2)) decoder_1 (
    .out0(decoder_1_out0), .out1(decoder_1_out1), .out2(decoder_1_out2), .out3(decoder_1_out3), .sel(IR[1:0]));
  Decoder #(.enable("false"), .select(2)) decoder_2 (
    .out0(decoder_2_out0), .out1(decoder_2_out1), .out2(decoder_2_out2), .out3(decoder_2_out3), .sel(IR[3:2]));
  and and_14 (and_14_out, step[4], IR[15]);
  and and_15 (and_15_out, step[5], ST);
  and and_16 (and_16_out, step[4], JMPR);
  and and_17 (and_17_out, step[4], IN_OUT, IR[3]);
  and and_18 (and_18_out, step[5], IR[15]);
  and and_19 (and_19_out, step[4], LD);
  and and_20 (and_20_out, step[4], ST);
  and and_21 (and_21_out, step[6], NOT_CMP, IR[15]);
  and and_22 (and_22_out, step[6], DATA);
  and and_23 (and_23_out, step[5], JCAEZ);
  and and_24 (and_24_out, step[5], LD);
  and and_25 (and_25_out, step[5], DATA);
  and and_26 (and_26_out, step[5], JMP);
  and and_27 (and_27_out, step[6], JCAEZ, CAEZ);
  and and_28 (and_28_out, step[4], DATA);
  and and_29 (and_29_out, step[4], JCAEZ);
  and and_30 (and_30_out, step[4], CLF);
  and and_31 (and_31_out, step[4], DATA);
  and and_32 (and_32_out, step[4], JMP);
  and and_33 (and_33_out, step[4], JCAEZ);
  clk clk_1 (.clk_e(clk_1_clk_e), .clk_s(clk_1_clk_s));
  and and_34 (to_ula[0], IR[12], step[5], IR[15]);
  and and_35 (to_ula[1], IR[13], step[5], IR[15]);
  and and_36 (to_ula[2], IR[14], step[5], IR[15]);
  stepper stepper_1 (
    .clk(clk_1_clk_e), .init(step[0]), .s1(step[1]), .s2(step[2]), .s3(step[3]), .s4(step[4]), .s5(step[5]),
    .s6(step[6]));
  not not_1 (not_1_out, IR[3]);
  Decoder #(.enable("false"), .select(3)) decoder_3 (
    .out0(decoder_3_out0[0]), .out1(decoder_3_out0[1]), .out2(decoder_3_out0[2]), .out3(decoder_3_out0[3]),
    .out4(decoder_3_out0[4]), .out5(decoder_3_out0[5]), .out6(decoder_3_out0[6]), .out7(decoder_3_out0[7]),
    .sel(IR[14:12]));
  not not_2 (not_2_out, IR[3]);
  not not_3 (not_3_out, IR[15]);
  and and_37 (LD, decoder_3_out0[0], not_3_out);
  and and_38 (ST, decoder_3_out0[1], not_3_out);
  and and_39 (DATA, decoder_3_out0[2], not_3_out);
  and and_40 (JMPR, decoder_3_out0[3], not_3_out);
  and and_41 (JMP, decoder_3_out0[4], not_3_out);
  and and_42 (JCAEZ, decoder_3_out0[5], not_3_out);
  and and_43 (CLF, decoder_3_out0[6], not_3_out);
  and and_44 (IN_OUT, decoder_3_out0[7], not_3_out);
  and and_45 (and_45_out, IR[12], IR[13], IR[14]);
  not not_4 (NOT_CMP, and_45_out);
  and and_46 (and_46_out, IR[3], C);
  and and_47 (and_47_out, IR[2], A);
  and and_48 (and_48_out, IR[1], E);
  and and_49 (and_49_out, IR[0], Z);
  and and_50 (and_50_out, step[5], IR[15]);
  and and_51 (and_51_out, step[4], DATA);
  and and_52 (and_52_out, step[4], JCAEZ);
  and and_53 (and_53_out, step[6], IR[15], NOT_CMP);
  and and_54 (and_54_out, step[5], LD);
  and and_55 (and_55_out, step[5], DATA);
  and and_56 (and_56_out, step[5], IN_OUT, not_2_out);
  and and_57 (and_57_out, step[4], LD);
  and and_58 (and_58_out, step[4], ST);
  and and_59 (and_59_out, step[4], DATA);
  and and_60 (and_60_out, step[4], JMP);
  and and_61 (and_61_out, step[4], JCAEZ);
  and and_62 (and_62_out, step[6], DATA);
  and and_63 (and_63_out, step[4], JMPR);
  and and_64 (and_64_out, step[5], JMP);
  and and_65 (and_65_out, step[5], JCAEZ);
  and and_66 (and_66_out, step[6], JCAEZ, CAEZ);
  and and_67 (and_67_out, step[4], CLF);
  and and_68 (and_68_out, step[5], IR[15]);
  or or_11 (CAEZ, and_46_out, and_47_out, and_48_out, and_49_out);
  and and_69 (and_69_out, step[5], ST);
  and and_70 (and_70_out, step[4], IN_OUT, IR[3]);
  Decoder #(.enable("false"), .select(2)) decoder_4 (
    .out0(decoder_4_out0), .out1(decoder_4_out1), .out2(decoder_4_out2), .out3(decoder_4_out3), .sel(IR[1:0]));
  and and_71 (and_71_out, step[4], IR[15]);
  or or_12 (or_12_out, and_50_out, and_51_out, and_52_out, step[1]);
  or or_13 (Reg_B_s, and_53_out, and_54_out, and_55_out, and_56_out);
  or or_14 (or_14_out, and_57_out, and_58_out, and_59_out, and_60_out, and_61_out, step[1]);
  or or_15 (or_15_out, and_62_out, and_63_out, and_64_out, and_65_out, and_66_out, step[3]);
  or or_16 (or_16_out, and_67_out, and_68_out);
  and and_72 (IR_s, step[2], clk_1_clk_s);
  and and_73 (TMP_s, and_71_out, clk_1_clk_s);
  and and_74 (ACC_s, or_12_out, clk_1_clk_s);
  and and_75 (MAR_s, or_14_out, clk_1_clk_s);
  and and_76 (RAM_s, and_69_out, clk_1_clk_s);
  and and_77 (IAR_s, or_15_out, clk_1_clk_s);
  and and_78 (FLAG_s, or_16_out, clk_1_clk_s);
  and and_79 (IO_clk_s, and_70_out, clk_1_clk_s);
  and and_80 (R0_s, clk_1_clk_s, Reg_B_s, decoder_4_out0);
  and and_81 (R1_s, clk_1_clk_s, Reg_B_s, decoder_4_out1);
  and and_82 (R2_s, clk_1_clk_s, Reg_B_s, decoder_4_out2);
  and and_83 (R3_s, clk_1_clk_s, Reg_B_s, decoder_4_out3);

  assign DATA_ADDR = IR[2];
  assign IO = IR[3];

  // Other names for the same wires on the sheet: DATA_ADDRESS = IR[2]; INPUT_OUTPUT = IR[3]; FLAG_A = A; FLAG_C = C;
  //   FLAG_E = E; FLAG_Z = Z; FLAGS_s = FLAG_s; I_O_clk_e = IO_clk_e; I_O_clk_s = IO_clk_s; FIRST_BIT_ON = IR[15];
  //   init = step[0]; s1 = step[1]; s2 = step[2]; s3 = step[3]; s4 = step[4]; s5 = step[5]; s6 = step[6]

  // Notes on the sheet:
  //   CONTROL UNIT
  //   init
  //   1
  //   2
  //   3
  //   4
  //   5
  //   6
endmodule

module stepper_alternativo (
  input  reset,
  input  clk,
  output init,
  output s1,
  output s2,
  output s3,
  output s4,
  output s5,
  output s6,
  output s7
);

  wire memoria_1bit_1_o, memoria_1bit_2_o, memoria_1bit_3_o, memoria_1bit_4_o, memoria_1bit_5_o,
       memoria_1bit_6_o, memoria_1bit_7_o, memoria_1bit_8_o, memoria_1bit_9_o, memoria_1bit_10_o,
       memoria_1bit_11_o, memoria_1bit_12_o, memoria_1bit_13_o, not_1_out, not_2_out, not_3_out, not_4_out,
       not_5_out, not_6_out, not_7_out, not_8_out, not_9_out, or_1_out, or_2_out;

  not not_1 (not_1_out, clk);
  not not_2 (not_2_out, reset);
  or or_1 (or_1_out, reset, not_1_out);
  or or_2 (or_2_out, reset, clk);
  or or_3 (init, reset, not_3_out);
  not not_3 (not_3_out, memoria_1bit_2_o);
  memoria_1bit memoria_1bit_1 (.i(not_2_out), .set(or_1_out), .o(memoria_1bit_1_o));
  memoria_1bit memoria_1bit_2 (.i(memoria_1bit_1_o), .set(or_2_out), .o(memoria_1bit_2_o));
  and and_1 (s1, memoria_1bit_2_o, not_4_out);
  not not_4 (not_4_out, memoria_1bit_4_o);
  memoria_1bit memoria_1bit_3 (.i(memoria_1bit_2_o), .set(or_1_out), .o(memoria_1bit_3_o));
  memoria_1bit memoria_1bit_4 (.i(memoria_1bit_3_o), .set(or_2_out), .o(memoria_1bit_4_o));
  and and_2 (s2, memoria_1bit_4_o, not_5_out);
  not not_5 (not_5_out, memoria_1bit_6_o);
  memoria_1bit memoria_1bit_5 (.i(memoria_1bit_4_o), .set(or_1_out), .o(memoria_1bit_5_o));
  memoria_1bit memoria_1bit_6 (.i(memoria_1bit_5_o), .set(or_2_out), .o(memoria_1bit_6_o));
  and and_3 (s3, memoria_1bit_6_o, not_6_out);
  memoria_1bit memoria_1bit_7 (.i(memoria_1bit_6_o), .set(or_1_out), .o(memoria_1bit_7_o));
  not not_6 (not_6_out, memoria_1bit_8_o);
  memoria_1bit memoria_1bit_8 (.i(memoria_1bit_7_o), .set(or_2_out), .o(memoria_1bit_8_o));
  and and_4 (s4, memoria_1bit_8_o, not_7_out);
  not not_7 (not_7_out, memoria_1bit_10_o);
  memoria_1bit memoria_1bit_9 (.i(memoria_1bit_8_o), .set(or_1_out), .o(memoria_1bit_9_o));
  memoria_1bit memoria_1bit_10 (.i(memoria_1bit_9_o), .set(or_2_out), .o(memoria_1bit_10_o));
  and and_5 (s5, memoria_1bit_10_o, not_8_out);
  not not_8 (not_8_out, memoria_1bit_12_o);
  memoria_1bit memoria_1bit_11 (.i(memoria_1bit_10_o), .set(or_1_out), .o(memoria_1bit_11_o));
  memoria_1bit memoria_1bit_12 (.i(memoria_1bit_11_o), .set(or_2_out), .o(memoria_1bit_12_o));
  and and_6 (s6, memoria_1bit_12_o, not_9_out);
  not not_9 (not_9_out, s7);
  memoria_1bit memoria_1bit_13 (.i(memoria_1bit_12_o), .set(or_1_out), .o(memoria_1bit_13_o));
  memoria_1bit memoria_1bit_14 (.i(memoria_1bit_13_o), .set(or_2_out), .o(s7));
endmodule

// FLAG
module flag (
  input  in_1,
  input  in_2,
  input  flag_s,
  input  in_4,
  input  in_5,
  output C,
  output A,
  output E,
  output Z
);

  Register #(.width(4)) register_1 (.D({in_5, in_4, in_2, in_1}), .Q({Z, E, A, C}), .clk(flag_s));  // open: en, clr
endmodule

module adaptador (
  input  IO_e,
  input  [15:0] from_bus,
  input  IO_s,
  input  D_A,
  input  I_O,
  input  [6:0] from_key,
  output [15:0] to_bus,
  output [6:0] to_tty,
  output clk_tty,
  output tty_on,
  output clear_buffer,
  output clk_key,
  output key_on,
  output [15:0] to_port_p,
  output clk_port_p,
  output port_p_on
);

  wire and_1_out, comparator_1_eq, comparator_2_eq, comparator_3_eq, comparator_4_eq;
  wire [15:0] bit_extender_1_out;

  and and_1 (and_1_out, IO_s, D_A, I_O);
  Comparator #(.width(16)) comparator_1 (.a(from_bus), .b({16{1'b0}}), .eq(comparator_1_eq));  // open: gt, lt
  Comparator #(.width(16)) comparator_2 (.a(from_bus), .b(16'h1), .eq(comparator_2_eq));  // open: gt, lt
  Comparator #(.width(16)) comparator_3 (.a(from_bus), .b(16'h2), .eq(comparator_3_eq));  // open: gt, lt
  Comparator #(.width(16)) comparator_4 (.a(from_bus), .b(16'hfffe), .eq(comparator_4_eq));  // open: gt, lt
  Register #(.width(1)) register_1 (.D(comparator_1_eq), .Q(key_on), .clk(and_1_out));  // open: en, clr
  Register #(.width(1)) register_2 (.D(comparator_2_eq), .Q(tty_on), .clk(and_1_out));  // open: en, clr
  Register #(.width(1)) register_3 (.D(comparator_3_eq), .Q(port_p_on), .clk(and_1_out));  // open: en, clr
  and and_2 (clear_buffer, comparator_4_eq, and_1_out);
  T_Flip_Flop t_ff_1 (.clk(IO_e), .T(1'b1), .Qn(clk_key));  // open: Q, preset, reset
  assign bit_extender_1_out = {{9{1'b0}}, from_key};  // Bit_Extender bit_extender_1
  Bit_Extender #(.in_width(16), .out_width(7), .\type ("zero")) bit_extender_2 (.in(from_bus), .out(to_tty));
  assign to_bus = IO_e ? bit_extender_1_out : 16'bz;  // Controlled_Buffer controlled_buffer_1

  assign clk_port_p = IO_s;
  assign clk_tty = IO_s;
  assign to_port_p = from_bus;
endmodule

module multi_8bits (
  input  [7:0] a_8bits,
  input  [7:0] b_8bits,
  output [7:0] o_8bits
);

  wire shl_1_p2, shl_2_p2, shl_10_p2, shl_19_p2, shl_21_p2, shl_26_p2, shl_28_p2, somador_8bits_1_p3,
       somador_8bits_2_p2, somador_8bits_2_p3, somador_8bits_3_p3, somador_8bits_4_p3, somador_8bits_5_p3,
       somador_8bits_6_p3;
  wire [7:0] repeat_0_1_out_3, repeat_0_2_out_3, repeat_0_3_out_3, repeat_0_4_out_3, repeat_0_5_out_3,
       repeat_0_6_out_3, repeat_0_7_out_3, repeat_0_8_out_3;
  wire [15:0] shl_3_p2, shl_4_p2, shl_5_p2, shl_6_p2, shl_7_p2, shl_9_out_3, shl_11_out_3, shl_12_out_3,
       shl_13_out_3, shl_14_out_3, shl_15_out_3, shl_16_out_3, shl_17_out_3, shl_18_out_3, shl_20_out_3,
       shl_22_out_3, shl_23_out_3, shl_24_out_3, shl_25_out_3, shl_27_out_3;

  repeat_0 repeat_0_1 (.in_1(a_8bits), .in_2(b_8bits[0]), .out_3(repeat_0_1_out_3));
  repeat_0 repeat_0_2 (.in_1(a_8bits), .in_2(b_8bits[1]), .out_3(repeat_0_2_out_3));
  repeat_0 repeat_0_3 (.in_1(a_8bits), .in_2(b_8bits[2]), .out_3(repeat_0_3_out_3));
  repeat_0 repeat_0_4 (.in_1(a_8bits), .in_2(b_8bits[3]), .out_3(repeat_0_4_out_3));
  repeat_0 repeat_0_5 (.in_1(a_8bits), .in_2(b_8bits[4]), .out_3(repeat_0_5_out_3));
  repeat_0 repeat_0_6 (.in_1(a_8bits), .in_2(b_8bits[5]), .out_3(repeat_0_6_out_3));
  repeat_0 repeat_0_7 (.in_1(a_8bits), .in_2(b_8bits[6]), .out_3(repeat_0_7_out_3));
  repeat_0 repeat_0_8 (.in_1(a_8bits), .in_2(b_8bits[7]), .out_3(repeat_0_8_out_3));
  // SHL shl_1: pin names not known; wires that end beside it: repeat_0_2_out_3, shl_1_p2
  // SHL shl_2: pin names not known; wires that end beside it: repeat_0_3_out_3, shl_2_p2
  // SHL shl_3: pin names not known; wires that end beside it: repeat_0_4_out_3, shl_3_p2
  // SHL shl_4: pin names not known; wires that end beside it: repeat_0_5_out_3, shl_4_p2
  // SHL shl_5: pin names not known; wires that end beside it: repeat_0_6_out_3, shl_5_p2
  // SHL shl_6: pin names not known; wires that end beside it: repeat_0_7_out_3, shl_6_p2
  // SHL shl_7: pin names not known; wires that end beside it: repeat_0_8_out_3, shl_7_p2
  // somador_8bits somador_8bits_1: pin names not known; wires that end beside it: repeat_0_1_out_3, shl_1_p2, somador_8bits_1_p3
  // somador_8bits somador_8bits_2: pin names not known; wires that end beside it: somador_8bits_1_p3, somador_8bits_2_p2, somador_8bits_2_p3
  // SHL shl_8: pin names not known; wires that end beside it: shl_2_p2, somador_8bits_2_p2
  SHL shl_9 (.in_2(shl_3_p2), .out_3(shl_9_out_3));  // open: c_in, c_out
  // SHL shl_10: pin names not known; wires that end beside it: shl_9_out_3, shl_10_p2
  SHL shl_11 (.in_2(shl_4_p2), .out_3(shl_11_out_3));  // open: c_in, c_out
  SHL shl_12 (.in_2(shl_11_out_3), .out_3(shl_12_out_3));  // open: c_in, c_out
  SHL shl_13 (.in_2(shl_5_p2), .out_3(shl_13_out_3));  // open: c_in, c_out
  SHL shl_14 (.in_2(shl_13_out_3), .out_3(shl_14_out_3));  // open: c_in, c_out
  SHL shl_15 (.in_2(shl_6_p2), .out_3(shl_15_out_3));  // open: c_in, c_out
  SHL shl_16 (.in_2(shl_15_out_3), .out_3(shl_16_out_3));  // open: c_in, c_out
  SHL shl_17 (.in_2(shl_7_p2), .out_3(shl_17_out_3));  // open: c_in, c_out
  SHL shl_18 (.in_2(shl_17_out_3), .out_3(shl_18_out_3));  // open: c_in, c_out
  // somador_8bits somador_8bits_3: pin names not known; wires that end beside it: somador_8bits_2_p3, shl_10_p2, somador_8bits_3_p3
  // SHL shl_19: pin names not known; wires that end beside it: shl_12_out_3, shl_19_p2
  SHL shl_20 (.in_2(shl_14_out_3), .out_3(shl_20_out_3));  // open: c_in, c_out
  // SHL shl_21: pin names not known; wires that end beside it: shl_20_out_3, shl_21_p2
  SHL shl_22 (.in_2(shl_16_out_3), .out_3(shl_22_out_3));  // open: c_in, c_out
  SHL shl_23 (.in_2(shl_22_out_3), .out_3(shl_23_out_3));  // open: c_in, c_out
  SHL shl_24 (.in_2(shl_18_out_3), .out_3(shl_24_out_3));  // open: c_in, c_out
  SHL shl_25 (.in_2(shl_24_out_3), .out_3(shl_25_out_3));  // open: c_in, c_out
  // somador_8bits somador_8bits_4: pin names not known; wires that end beside it: somador_8bits_3_p3, shl_19_p2, somador_8bits_4_p3
  // somador_8bits somador_8bits_5: pin names not known; wires that end beside it: somador_8bits_4_p3, shl_21_p2, somador_8bits_5_p3
  // SHL shl_26: pin names not known; wires that end beside it: shl_23_out_3, shl_26_p2
  SHL shl_27 (.in_2(shl_25_out_3), .out_3(shl_27_out_3));  // open: c_in, c_out
  // SHL shl_28: pin names not known; wires that end beside it: shl_27_out_3, shl_28_p2
  // somador_8bits somador_8bits_6: pin names not known; wires that end beside it: somador_8bits_5_p3, shl_26_p2, somador_8bits_6_p3
  // somador_8bits somador_8bits_7: pin names not known; wires that end beside it: somador_8bits_6_p3, shl_28_p2, o_8bits
endmodule

module repeat_0 (
  input  [7:0] in_1,
  input  in_2,
  output [7:0] out_3
);

  Multiplexer #(.width(8)) multiplexer_1 (.in0({8{1'b0}}), .in1(in_1), .out(out_3), .sel(in_2));
endmodule

module somador_16bits (
  input  c_in,
  input  [15:0] a_16bit,
  input  [15:0] b_16bit,
  output [15:0] o_16bit,
  output c_out
);

  wire somador_completo_1bit_1_c_out, somador_completo_1bit_2_c_out, somador_completo_1bit_3_c_out,
       somador_completo_1bit_4_c_out, somador_completo_1bit_5_c_out, somador_completo_1bit_6_c_out,
       somador_completo_1bit_7_c_out, somador_completo_1bit_8_c_out, somador_completo_1bit_9_c_out,
       somador_completo_1bit_10_c_out, somador_completo_1bit_11_c_out, somador_completo_1bit_12_c_out,
       somador_completo_1bit_13_c_out, somador_completo_1bit_14_c_out, somador_completo_1bit_15_c_out;

  somador_completo_1bit somador_completo_1bit_1 (
    .a(a_16bit[0]), .b(b_16bit[0]), .c_in(c_in), .c_out(somador_completo_1bit_1_c_out), .o(o_16bit[0]));
  somador_completo_1bit somador_completo_1bit_2 (
    .a(a_16bit[1]), .b(b_16bit[1]), .c_in(somador_completo_1bit_1_c_out),
    .c_out(somador_completo_1bit_2_c_out), .o(o_16bit[1]));
  somador_completo_1bit somador_completo_1bit_3 (
    .a(a_16bit[2]), .b(b_16bit[2]), .c_in(somador_completo_1bit_2_c_out),
    .c_out(somador_completo_1bit_3_c_out), .o(o_16bit[2]));
  somador_completo_1bit somador_completo_1bit_4 (
    .a(a_16bit[3]), .b(b_16bit[3]), .c_in(somador_completo_1bit_3_c_out),
    .c_out(somador_completo_1bit_4_c_out), .o(o_16bit[3]));
  somador_completo_1bit somador_completo_1bit_5 (
    .a(a_16bit[4]), .b(b_16bit[4]), .c_in(somador_completo_1bit_4_c_out),
    .c_out(somador_completo_1bit_5_c_out), .o(o_16bit[4]));
  somador_completo_1bit somador_completo_1bit_6 (
    .a(a_16bit[5]), .b(b_16bit[5]), .c_in(somador_completo_1bit_5_c_out),
    .c_out(somador_completo_1bit_6_c_out), .o(o_16bit[5]));
  somador_completo_1bit somador_completo_1bit_7 (
    .a(a_16bit[6]), .b(b_16bit[6]), .c_in(somador_completo_1bit_6_c_out),
    .c_out(somador_completo_1bit_7_c_out), .o(o_16bit[6]));
  somador_completo_1bit somador_completo_1bit_8 (
    .a(a_16bit[7]), .b(b_16bit[7]), .c_in(somador_completo_1bit_7_c_out),
    .c_out(somador_completo_1bit_8_c_out), .o(o_16bit[7]));
  somador_completo_1bit somador_completo_1bit_9 (
    .a(a_16bit[8]), .b(b_16bit[8]), .c_in(somador_completo_1bit_8_c_out),
    .c_out(somador_completo_1bit_9_c_out), .o(o_16bit[8]));
  somador_completo_1bit somador_completo_1bit_10 (
    .a(a_16bit[9]), .b(b_16bit[9]), .c_in(somador_completo_1bit_9_c_out),
    .c_out(somador_completo_1bit_10_c_out), .o(o_16bit[9]));
  somador_completo_1bit somador_completo_1bit_11 (
    .a(a_16bit[10]), .b(b_16bit[10]), .c_in(somador_completo_1bit_10_c_out),
    .c_out(somador_completo_1bit_11_c_out), .o(o_16bit[10]));
  somador_completo_1bit somador_completo_1bit_12 (
    .a(a_16bit[11]), .b(b_16bit[11]), .c_in(somador_completo_1bit_11_c_out),
    .c_out(somador_completo_1bit_12_c_out), .o(o_16bit[11]));
  somador_completo_1bit somador_completo_1bit_13 (
    .a(a_16bit[12]), .b(b_16bit[12]), .c_in(somador_completo_1bit_12_c_out),
    .c_out(somador_completo_1bit_13_c_out), .o(o_16bit[12]));
  somador_completo_1bit somador_completo_1bit_14 (
    .a(a_16bit[13]), .b(b_16bit[13]), .c_in(somador_completo_1bit_13_c_out),
    .c_out(somador_completo_1bit_14_c_out), .o(o_16bit[13]));
  somador_completo_1bit somador_completo_1bit_15 (
    .a(a_16bit[14]), .b(b_16bit[14]), .c_in(somador_completo_1bit_14_c_out),
    .c_out(somador_completo_1bit_15_c_out), .o(o_16bit[14]));
  somador_completo_1bit somador_completo_1bit_16 (
    .a(a_16bit[15]), .b(b_16bit[15]), .c_in(somador_completo_1bit_15_c_out), .c_out(c_out), .o(o_16bit[15]));
endmodule
